# Fritzing sketch Schaltbild_SARA (saved by Fritzing 0.9.6b)
breadboards: 1

parts:
  R1 = Resistor [tolerance=±5% power=0.25 resistance=100k package=THT]
  R2 = Resistor [tolerance=±5% power=0.25 resistance=100k package=THT]
  Sara = Arduino Nano 33 BLE Sense

nets:
  BAT_GND/DHT_GND/RAIN_GAUGE/WIND_GND: R1.Pin_0, Sara.GND, Sara.A7
  N1: R1.Pin_1, R2.Pin_0, Sara.A4
  V_BAT: R2.Pin_1
  RAIN_GAUGE_VCC/WIND_VCC: Sara.D11/MOSI, Sara.+5V
  BAT_REGULATOR_5V: Sara.VIN
  WIND_SPEED: Sara.A6
  WIND_DIRECTION: Sara.A5
  DHT_SIGNAL: Sara.A3
  DHT_VCC: Sara.3V3

custom parts:
  Arduino Nano 33 BLE Sense: The Nano 33 BLE Sense (without headers) is Arduino’s 3.3V AI enabled board in the smallest available form factor: 45x18mm! The Arduino Nano 33 BLE Sense is a completely new board on a well-known form factor. It comes with a series of embedded sensors: 9 axis inertial sensor: what makes this board ideal for wearable devices humidity, and temperature sensor: to get highly accurate measurements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
